// Logisim project Control_Unit.circ as structural Verilog
module Control_Unit (
  input  START,
  input  FETCHED,
  input  EXECUTED,
  input  HALT,
  input  RESET,
  input  [3:0] Instruction_Type,
  output fetch,
  output reset_2
);

  wire clk, demultiplexer_1_out0, demultiplexer_2_out0, demultiplexer_2_out1, demultiplexer_3_out0,
       demultiplexer_3_out1, demultiplexer_4_out0, demultiplexer_4_out1, END_q, EXEC_q, FETCH_q, IDLE_q,
       or_1_out, or_2_out, or_3_out, or_4_out;

  Clock clock_1 (.out(clk));
  or or_1 (or_1_out, demultiplexer_1_out0, 1'b1);
  Demultiplexer #(.enable("false")) demultiplexer_1 (
    .out0(demultiplexer_1_out0), .out1(fetch), .in(IDLE_q), .sel(START));
  D_Flip_Flop IDLE (.clk(or_1_out), .D(clk), .Q(IDLE_q), .preset(1'b1));  // open: Qn, en, reset
  or or_2 (or_2_out, demultiplexer_2_out0, demultiplexer_4_out1, fetch);
  D_Flip_Flop u_FETCH (.clk(or_2_out), .D(clk), .Q(FETCH_q), .preset(1'b1));  // open: Qn, en, reset
  Demultiplexer #(.enable("false")) demultiplexer_2 (
    .out0(demultiplexer_2_out0), .out1(demultiplexer_2_out1), .in(FETCH_q), .sel(FETCHED));
  Demultiplexer #(.enable("false")) demultiplexer_3 (
    .out0(demultiplexer_3_out0), .out1(demultiplexer_3_out1), .in(demultiplexer_2_out1), .sel(HALT));
  or or_3 (or_3_out, demultiplexer_4_out0, demultiplexer_3_out0);
  D_Flip_Flop EXEC (.clk(or_3_out), .D(clk), .Q(EXEC_q), .preset(1'b1));  // open: Qn, en, reset
  Demultiplexer #(.enable("false")) demultiplexer_4 (
    .out0(demultiplexer_4_out0), .out1(demultiplexer_4_out1), .in(EXEC_q), .sel(EXECUTED));
  or or_4 (or_4_out, END_q, demultiplexer_3_out1);
  D_Flip_Flop END (.clk(or_4_out), .D(clk), .Q(END_q), .preset(1'b1));  // open: Qn, en, reset

  assign reset_2 = RESET;

  // Other names for the same wires on the sheet: Ins_Type[3:0] = Instruction_Type; rst = RESET
endmodule
